# Fritzing sketch wiring-diagram (saved by Fritzing 0.9.4)
breadboards: 1

parts:
  Part1 = Arduino Uno (Rev3)
  LCD1 = LCD screen
  CUI-enc1 = AMT103
  R1 = Resistor [tolerance=±5% resistance=10 package=THT]
  ZS-042_RTC1 = ZS-042 RTC Module

nets (from the schematic view):
  N1: Part1.A4/SDA, ZS-042_RTC1.SDA
  N2: Part1.A5/SCL, ZS-042_RTC1.SCL
  N3: Part1.D8, LCD1.E
  N4: Part1.D9_PWM, LCD1.DB4
  N5: Part1.D10_PWM/SS, LCD1.DB5
  N6: Part1.D11_PWM/MOSI, LCD1.DB6
  N7: Part1.D12/MISO, LCD1.DB7
  N8: Part1.D13/SCK, CUI-enc1.B
  N9: Part1.D2, CUI-enc1.X
  N10: Part1.D3_PWM, LCD1.LED+
  N11: Part1.D4, CUI-enc1.A
  N12: Part1.D6_PWM, R1.Pin_1
  N13: Part1.D7, LCD1.RS
  5V: Part1.5V, LCD1.VDD, CUI-enc1.5V, ZS-042_RTC1.VCC
  GND: Part1.GND, LCD1.VSS, LCD1.R/W, LCD1.LED-, CUI-enc1.GND, ZS-042_RTC1.GND
  N14: LCD1.V0, R1.Pin_0
